// Digital circuit Template.dig as structural Verilog
module Template (
  input  A,
  input  B,
  output Output,
  output Output_2
);

  wire and_1_out, and_2_out, not_1_out, not_2_out, not_3_out, not_4_out, or_1_out, or_2_out;

  not not_1 (not_1_out, A);
  not not_2 (not_2_out, B);
  not not_3 (not_3_out, A);
  not not_4 (not_4_out, B);
  and and_1 (and_1_out, not_1_out, B);
  and and_2 (and_2_out, A, not_2_out);
  or or_1 (or_1_out, not_3_out, not_4_out);
  or or_2 (or_2_out, A, B);
  or or_3 (Output, and_1_out, and_2_out);
  and and_3 (Output_2, or_1_out, or_2_out);
endmodule
