// Digital circuit Template.dig as structural Verilog
module Template (
  input  A,
  input  B,
  output Output
);

  wire A_t, B_t, not_1_out, not_2_out, or_1_out, or_2_out;

  not not_1 (not_1_out, A_t);
  not not_2 (not_2_out, B_t);
  or or_1 (or_1_out, not_1_out, not_2_out);
  or or_2 (or_2_out, A_t, B_t);
  and and_1 (Output, or_1_out, or_2_out);
endmodule
