// Digital circuit Template.dig as structural Verilog
module Template (
  input  A,
  input  B,
  input  Cin,
  output Sum,
  output Cout,
  output Sum_2,
  output Cout_2
);

  wire and_1_out, and_2_out, and_3_out, and_4_out, and_6_out, and_7_out, and_8_out, and_9_out, not_1_out,
       not_2_out, not_3_out, not_4_out, not_5_out, not_6_out, not_7_out, not_8_out, not_9_out, not_10_out,
       not_11_out, not_12_out, not_13_out, not_14_out, not_15_out, not_16_out, not_17_out, not_18_out,
       or_1_out, or_2_out, or_3_out, or_4_out, or_6_out, or_7_out, or_8_out, or_9_out;

  not not_1 (not_1_out, A);
  not not_2 (not_2_out, B);
  not not_3 (not_3_out, A);
  not not_4 (not_4_out, Cin);
  not not_5 (not_5_out, B);
  not not_6 (not_6_out, Cin);
  not not_7 (not_7_out, B);
  not not_8 (not_8_out, Cin);
  not not_9 (not_9_out, A);
  not not_10 (not_10_out, Cin);
  not not_11 (not_11_out, A);
  not not_12 (not_12_out, B);
  and and_1 (and_1_out, not_1_out, not_2_out, Cin);
  and and_2 (and_2_out, not_3_out, B, not_4_out);
  and and_3 (and_3_out, A, not_5_out, not_6_out);
  and and_4 (and_4_out, A, B, Cin);
  or or_1 (or_1_out, A, B, Cin);
  or or_2 (or_2_out, A, not_7_out, not_8_out);
  or or_3 (or_3_out, not_9_out, B, not_10_out);
  or or_4 (or_4_out, not_11_out, not_12_out, Cin);
  or or_5 (Sum, and_1_out, and_2_out, and_3_out, and_4_out);
  and and_5 (Sum_2, or_1_out, or_2_out, or_3_out, or_4_out);
  not not_13 (not_13_out, A);
  not not_14 (not_14_out, B);
  not not_15 (not_15_out, Cin);
  not not_16 (not_16_out, Cin);
  not not_17 (not_17_out, B);
  not not_18 (not_18_out, A);
  and and_6 (and_6_out, not_13_out, B, Cin);
  and and_7 (and_7_out, A, not_14_out, Cin);
  and and_8 (and_8_out, A, B, not_15_out);
  and and_9 (and_9_out, A, B, Cin);
  or or_6 (or_6_out, A, B, Cin);
  or or_7 (or_7_out, A, B, not_16_out);
  or or_8 (or_8_out, A, not_17_out, Cin);
  or or_9 (or_9_out, not_18_out, B, Cin);
  or or_10 (Cout, and_6_out, and_7_out, and_8_out, and_9_out);
  and and_10 (Cout_2, or_6_out, or_7_out, or_8_out, or_9_out);
endmodule
