// Digital circuit Template.dig as structural Verilog
module Template (
  input  A,
  input  B,
  input  C,
  input  D,
  output Z1,
  output Z2,
  output Z3,
  output Z3_2,
  output Z1_2,
  output Z2_2
);

  wire and_1_out, and_2_out, and_3_out, and_4_out, and_5_out, and_6_out, and_7_out, and_8_out, and_9_out,
       and_10_out, not_1_out, not_2_out, not_3_out, not_4_out, not_5_out, not_6_out, not_7_out, not_8_out,
       not_9_out, not_10_out, not_11_out, not_12_out, not_13_out, not_14_out, not_15_out, not_16_out,
       not_17_out, not_18_out, not_19_out, not_20_out, not_21_out, not_22_out, not_23_out, not_24_out,
       not_25_out, not_26_out, not_27_out, not_28_out, not_29_out, not_30_out, not_31_out, or_4_out,
       or_5_out, or_6_out, or_7_out, or_8_out, or_9_out, or_10_out, or_11_out, or_12_out, or_13_out,
       or_14_out, or_15_out, or_16_out;

  not not_1 (not_1_out, C);
  not not_2 (not_2_out, D);
  not not_3 (not_3_out, C);
  not not_4 (not_4_out, D);
  not not_5 (not_5_out, A);
  not not_6 (not_6_out, A);
  not not_7 (not_7_out, B);
  not not_8 (not_8_out, B);
  not not_9 (not_9_out, A);
  not not_10 (not_10_out, B);
  not not_11 (not_11_out, C);
  not not_12 (not_12_out, D);
  not not_13 (not_13_out, A);
  not not_14 (not_14_out, C);
  not not_15 (not_15_out, B);
  and and_1 (and_1_out, A, not_1_out);
  and and_2 (and_2_out, A, B, not_2_out);
  and and_3 (and_3_out, B, not_3_out, not_4_out);
  and and_4 (and_4_out, not_5_out, C);
  and and_5 (and_5_out, not_6_out, not_7_out, D);
  and and_6 (and_6_out, not_8_out, C, D);
  and and_7 (and_7_out, not_9_out, not_10_out, not_11_out, not_12_out);
  and and_8 (and_8_out, not_13_out, B, not_14_out, D);
  and and_9 (and_9_out, A, not_15_out, C, D);
  and and_10 (and_10_out, A, B, C, D);
  or or_1 (Z1, and_1_out, and_2_out, and_3_out);
  or or_2 (Z2, and_4_out, and_5_out, and_6_out);
  or or_3 (Z3, and_7_out, and_8_out, and_9_out, and_10_out);
  not not_16 (not_16_out, D);
  not not_17 (not_17_out, C);
  not not_18 (not_18_out, D);
  not not_19 (not_19_out, B);
  not not_20 (not_20_out, C);
  not not_21 (not_21_out, A);
  not not_22 (not_22_out, C);
  not not_23 (not_23_out, A);
  not not_24 (not_24_out, B);
  not not_25 (not_25_out, A);
  not not_26 (not_26_out, B);
  not not_27 (not_27_out, A);
  not not_28 (not_28_out, C);
  not not_29 (not_29_out, D);
  not not_30 (not_30_out, B);
  not not_31 (not_31_out, C);
  or or_4 (or_4_out, A, B);
  or or_5 (or_5_out, A, not_16_out);
  or or_6 (or_6_out, not_17_out, not_18_out);
  or or_7 (or_7_out, A, not_19_out, not_20_out);
  or or_8 (or_8_out, not_21_out, B, not_22_out);
  or or_9 (or_9_out, not_23_out, C);
  or or_10 (or_10_out, not_24_out, C);
  or or_11 (or_11_out, C, D);
  or or_12 (or_12_out, not_25_out, not_26_out);
  or or_13 (or_13_out, not_27_out, B, D);
  or or_14 (or_14_out, A, not_28_out);
  or or_15 (or_15_out, A, B, not_29_out);
  or or_16 (or_16_out, not_30_out, not_31_out, D);
  and and_11 (Z1_2, or_4_out, or_5_out, or_6_out, or_7_out, or_8_out);
  and and_12 (Z2_2, or_9_out, or_10_out, or_11_out, or_12_out, or_13_out);
  and and_13 (Z3_2, or_14_out, or_15_out, or_16_out);
endmodule
