// Digital circuit Template.dig as structural Verilog
module Template (
  input  [3:0] In,
  output A,
  output B,
  output C,
  output D,
  output E,
  output F,
  output G
);

  wire or_1_out, or_2_out, or_3_out, or_4_out, or_6_out, or_7_out, or_8_out, or_9_out, or_10_out, or_11_out,
       or_12_out, or_13_out, W_t, X_t, Y_t, Z_t;

  or or_1 (or_1_out, In[3], In[2], In[1], Z_t);
  or or_2 (or_2_out, X_t, In[1], In[0]);
  or or_3 (or_3_out, X_t, Y_t, In[0]);
  or or_4 (or_4_out, X_t, In[1], Z_t);
  or or_5 (C, In[2], Y_t, In[0]);
  or or_6 (or_6_out, In[3], In[2], In[1], Z_t);
  or or_7 (or_7_out, X_t, Y_t, Z_t);
  or or_8 (or_8_out, X_t, In[1], In[0]);
  or or_9 (or_9_out, X_t, In[1], In[0]);
  or or_10 (or_10_out, In[3], In[2], In[1], Z_t);
  or or_11 (or_11_out, In[2], Y_t);
  or or_12 (or_12_out, In[3], In[2], In[1]);
  or or_13 (or_13_out, X_t, Y_t, Z_t);
  and and_1 (A, or_1_out, or_2_out);
  and and_2 (B, or_3_out, or_4_out);
  and and_3 (E, or_9_out, Z_t);
  and and_4 (F, or_10_out, or_11_out);
  and and_5 (G, or_12_out, or_13_out);
  not not_1 (Z_t, In[0]);
  and and_6 (D, or_6_out, or_7_out, or_8_out);
  not not_2 (Y_t, In[1]);
  not not_3 (X_t, In[2]);
  Seven_Seg seven_seg_1 (.a(A), .b(B), .c(C), .d(D), .e(E), .f(F), .g(G), .dp(1'b0));
  not not_4 (W_t, In[3]);

  // Other names for the same wires on the sheet: Z = In[0]; Y = In[1]; X = In[2]; W = In[3]
endmodule
