// Digital circuit Template.dig as structural Verilog
module Template (
  input  [2:0] In,
  input  clk,
  output [7:0] Z
);

  wire i0_t, i1_t, i2_t, or_1_out, or_2_out, or_3_out, or_4_out, or_5_out, or_6_out, or_8_out, or_9_out,
       or_10_out, or_11_out, or_12_out, or_13_out, or_14_out, or_15_out, or_16_out, or_17_out, or_18_out,
       or_19_out;

  or or_1 (or_1_out, i2_t, In[1], i0_t);
  or or_2 (or_2_out, In[2], i1_t, i0_t);
  or or_3 (or_3_out, In[2], In[1], In[0]);
  or or_4 (or_4_out, i2_t, i1_t, In[0]);
  or or_5 (or_5_out, In[2], In[1], i0_t);
  or or_6 (or_6_out, i2_t, i1_t, i0_t);
  not not_1 (i0_t, In[0]);
  and and_1 (Z[5], or_1_out, or_2_out, or_3_out);
  and and_2 (Z[2], or_4_out, or_5_out, or_6_out);
  not not_2 (i1_t, In[1]);
  or or_7 (Z[6], In[0], i0_t);
  not not_3 (i2_t, In[2]);
  or or_8 (or_8_out, i1_t, In[0]);
  or or_9 (or_9_out, i2_t, i1_t, i0_t);
  or or_10 (or_10_out, In[2], In[1], In[0]);
  or or_11 (or_11_out, i2_t, i1_t, In[0]);
  or or_12 (or_12_out, In[2], In[1], i0_t);
  or or_13 (or_13_out, i2_t, In[1], i0_t);
  or or_14 (or_14_out, In[2], i1_t, i0_t);
  or or_15 (or_15_out, In[2], In[1], In[0]);
  and and_3 (Z[3], or_8_out, or_9_out, or_10_out);
  and and_4 (Z[1], or_11_out, or_12_out, or_13_out, or_14_out, or_15_out);
  Terminal terminal_1 (.D({1'b0, Z[6:5], 1'b0, Z[3:0]}), .C(clk), .en(1'b1));
  or or_16 (or_16_out, i2_t, i1_t, i0_t);
  or or_17 (or_17_out, i2_t, In[1], i0_t);
  or or_18 (or_18_out, In[2], i1_t, i0_t);
  or or_19 (or_19_out, In[2], In[1], In[0]);
  and and_5 (Z[0], or_16_out, or_17_out, or_18_out, or_19_out);

  assign {Z[7], Z[4]} = 2'b00;

  // Other names for the same wires on the sheet: B = Z[6]; C = Z[5]; E = Z[3]; F = Z[2]; G = Z[1]; H = Z[0];
  //   i0 = In[0]; i1 = In[1]; i2 = In[2]
endmodule
