// Digital circuit 2421.dig as structural Verilog
module _2421 (
  input  [3:0] In,
  output t3,
  output t2,
  output t1,
  output t0
);

  wire i0b, i1b, i2b, i3b, or_1_out, or_2_out, or_3_out, or_4_out, or_5_out, or_6_out, or_7_out, or_8_out,
       or_9_out, or_10_out, or_11_out, or_12_out, or_13_out, or_14_out, or_15_out;

  not not_1 (i0b, In[0]);
  or or_1 (or_1_out, i2b, In[1], In[0]);
  or or_2 (or_2_out, In[3], In[2], In[1]);
  or or_3 (or_3_out, In[2], i1b);
  or or_4 (or_4_out, i3b, i2b);
  or or_5 (or_5_out, i2b, In[1], i0b);
  or or_6 (or_6_out, In[3], In[2], In[1]);
  or or_7 (or_7_out, In[2], i1b);
  or or_8 (or_8_out, i3b, i2b);
  or or_9 (or_9_out, i2b, In[1], In[0]);
  or or_10 (or_10_out, In[3], In[2], In[1]);
  or or_11 (or_11_out, i2b, i1b);
  or or_12 (or_12_out, i3b, i1b);
  or or_13 (or_13_out, i3b, i2b);
  or or_14 (or_14_out, i3b, i1b);
  or or_15 (or_15_out, i3b, i2b);
  not not_2 (i1b, In[1]);
  and and_1 (t0, In[0], or_14_out, or_15_out);
  and and_2 (t3, or_1_out, or_2_out, or_3_out, or_4_out);
  and and_3 (t2, or_5_out, or_6_out, or_7_out, or_8_out);
  and and_4 (t1, or_9_out, or_10_out, or_11_out, or_12_out, or_13_out);
  not not_3 (i2b, In[2]);
  not not_4 (i3b, In[3]);

  // Other names for the same wires on the sheet: i0 = In[0]; i1 = In[1]; i2 = In[2]; i3 = In[3]
endmodule
