// Digital circuit 642neg3.dig as structural Verilog
module _642neg3 (
  input  [3:0] In,
  output s3,
  output s2,
  output s1,
  output s0
);

  wire i0b, i1b, i2b, i3b, or_1_out, or_2_out, or_3_out, or_4_out, or_5_out, or_6_out, or_7_out, or_8_out,
       or_9_out, or_10_out, or_11_out, or_12_out, or_13_out, or_14_out, or_15_out, or_16_out, or_17_out,
       or_18_out, or_19_out;

  not not_1 (i0b, In[0]);
  or or_1 (or_1_out, In[3], In[2], In[1]);
  or or_2 (or_2_out, i2b, In[1], In[0]);
  or or_3 (or_3_out, i1b, In[0]);
  or or_4 (or_4_out, i3b, i1b);
  or or_5 (or_5_out, i3b, i2b);
  or or_6 (or_6_out, i2b, In[1], i0b);
  or or_7 (or_7_out, In[2], i1b);
  or or_8 (or_8_out, In[2], In[0]);
  or or_9 (or_9_out, i3b, i2b);
  or or_10 (or_10_out, In[3], In[2], In[1]);
  or or_11 (or_11_out, i1b, i0b);
  or or_12 (or_12_out, i2b, In[1], In[0]);
  or or_13 (or_13_out, i3b, i1b);
  or or_14 (or_14_out, i3b, i2b);
  or or_15 (or_15_out, In[2], In[0]);
  or or_16 (or_16_out, i2b, In[1], In[0]);
  or or_17 (or_17_out, i1b, In[0]);
  or or_18 (or_18_out, i3b, i1b);
  or or_19 (or_19_out, i3b, i2b);
  not not_2 (i1b, In[1]);
  and and_1 (s3, or_1_out, or_2_out, or_3_out, or_4_out, or_5_out);
  and and_2 (s2, or_6_out, or_7_out, or_8_out, or_9_out);
  and and_3 (s1, or_10_out, or_11_out, or_12_out, or_13_out, or_14_out);
  and and_4 (s0, or_15_out, or_16_out, or_17_out, or_18_out, or_19_out);
  not not_3 (i2b, In[2]);
  not not_4 (i3b, In[3]);

  // Other names for the same wires on the sheet: i0 = In[0]; i1 = In[1]; i2 = In[2]; i3 = In[3]
endmodule
