// Digital circuit Templatet.dig as structural Verilog
module Templatet (
  input  [3:0] In,
  input  [1:0] Selector,
  output [3:0] Output
);

  wire C0, C1, C2, C3, E0, E1, E2, E3, i0b, i1b, i2b, i3b, S0, s0b, S1, s1b, S2, S3, T0, T1, T2, T3;

  excess3 excess3_1 (.In(In), .e3(E3), .e2(E2), .e1(E1), .e0(E0));
  cyclic cyclic_1 (.In(In), .c3(C3), .c2(C2), .c1(C1), .c0(C0));
  _2421 _2421_1 (.In(In), .t3(T3), .t2(T2), .t1(T1), .t0(T0));
  _642neg3 _642neg3_1 (.In(In), .s3(S3), .s2(S2), .s1(S1), .s0(S0));
  not not_1 (i0b, In[0]);
  not not_2 (s0b, Selector[0]);
  not not_3 (i1b, In[1]);
  not not_4 (s1b, Selector[1]);
  not not_5 (i2b, In[2]);
  Multiplexer #(.Selector_Bits(2)) multiplexer_1 (
    .sel(Selector), .in_0(E3), .in_1(C3), .in_2(T3), .in_3(S3), .out(Output[3]));
  Multiplexer #(.Selector_Bits(2)) multiplexer_2 (
    .sel(Selector), .in_0(E2), .in_1(C2), .in_2(T2), .in_3(S2), .out(Output[2]));
  Multiplexer #(.Selector_Bits(2)) multiplexer_3 (
    .sel(Selector), .in_0(E1), .in_1(C1), .in_2(T1), .in_3(S1), .out(Output[1]));
  not not_6 (i3b, In[3]);
  Multiplexer #(.Selector_Bits(2)) multiplexer_4 (
    .sel(Selector), .in_0(E0), .in_1(C0), .in_2(T0), .in_3(S0), .out(Output[0]));

  // Other names for the same wires on the sheet: i0 = In[0]; i1 = In[1]; i2 = In[2]; i3 = In[3]; s0_t = Selector[0];
  //   s1_t = Selector[1]; W = Output[3]; X = Output[2]; Y = Output[1]; Z = Output[0]
endmodule
