// Digital circuit HammingCode.dig as structural Verilog
module HammingCode (
  input  [6:0] In,
  output c1,
  output c2,
  output c3
);

  wire i0b, i1b, i2b, i3b, i4b, i5b, i6b, xor_1_out, xor_2_out, xor_3_out, xor_4_out, xor_5_out, xor_6_out;

  not not_1 (i0b, In[0]);
  xor xor_1 (xor_1_out, In[0], In[1]);
  xor xor_2 (xor_2_out, In[0], In[1]);
  xor xor_3 (xor_3_out, In[0], In[2]);
  not not_2 (i1b, In[1]);
  xor xor_4 (xor_4_out, xor_1_out, In[2]);
  xor xor_5 (xor_5_out, xor_2_out, In[4]);
  xor xor_6 (xor_6_out, xor_3_out, In[4]);
  not not_3 (i2b, In[2]);
  xor xor_7 (c1, xor_4_out, In[3]);
  xor xor_8 (c2, xor_5_out, In[5]);
  xor xor_9 (c3, xor_6_out, In[6]);
  not not_4 (i3b, In[3]);
  not not_5 (i4b, In[4]);
  not not_6 (i5b, In[5]);
  not not_7 (i6b, In[6]);

  // Other names for the same wires on the sheet: i0 = In[0]; i1 = In[1]; i2 = In[2]; i3 = In[3]; i4 = In[4];
  //   i5 = In[5]; i6 = In[6]
endmodule
