// Digital circuit Invertcircuit.dig as structural Verilog
module Invertcircuit (
  input  C1,
  input  C2,
  input  C3,
  output [6:0] Ball
);

  wire C1b, C2b, C3b;

  and and_1 (Ball[0], C1, C2, C3);
  and and_2 (Ball[1], C1, C2, C3b);
  and and_3 (Ball[2], C1, C2b, C3);
  and and_4 (Ball[3], C1, C2b, C3b);
  and and_5 (Ball[4], C1b, C2, C3);
  and and_6 (Ball[5], C1b, C2, C3b);
  and and_7 (Ball[6], C1b, C2b, C3);
  not not_1 (C1b, C1);
  not not_2 (C2b, C2);
  not not_3 (C3b, C3);

  // Other names for the same wires on the sheet: B0 = Ball[0]; B1 = Ball[1]; B2 = Ball[2]; B3 = Ball[3]; B4 = Ball[4];
  //   B5 = Ball[5]; B6 = Ball[6]
endmodule
