// Digital circuit Template.dig as structural Verilog
module Template (
  input  [6:0] In,
  output [6:0] Output
);

  wire hammingcode_1_c1, hammingcode_1_c2, hammingcode_1_c3;
  wire [6:0] invertcircuit_1_ball;

  HammingCode hammingcode_1 (.In(In), .c1(hammingcode_1_c1), .c2(hammingcode_1_c2), .c3(hammingcode_1_c3));
  Invertcircuit invertcircuit_1 (
    .C1(hammingcode_1_c1), .C2(hammingcode_1_c2), .C3(hammingcode_1_c3), .Ball(invertcircuit_1_ball));
  Ccircuit ccircuit_1 (.i0(invertcircuit_1_ball), .i1(In), .out(Output));
endmodule
