// Digital circuit Template.dig as structural Verilog
module Template (
  input  A,
  input  B,
  input  C,
  input  D,
  output Before,
  output After
);

  wire and_1_out, and_2_out, and_3_out, and_4_out;

  and and_1 (and_1_out, ~B, A, D);  // And
  and and_2 (and_2_out, ~C, D);  // And
  or or_1 (Before, ~A, and_1_out, and_2_out);  // Or
  and and_3 (and_3_out, ~B, D);  // And
  and and_4 (and_4_out, ~C, D);  // And
  or or_2 (After, ~A, and_3_out, and_4_out);  // Or
endmodule
