// Digital circuit Template.dig as structural Verilog
module Template (
  input  A,
  input  B,
  input  C,
  input  D,
  input  E,
  input  F,
  output After,
  output Before
);

  wire Ab, and_1_out, and_2_out, and_3_out, and_4_out, and_5_out, and_6_out, and_7_out, and_8_out, Bb, Cb,
       Db, Eb, Fb;

  and and_1 (and_1_out, Ab, Bb, E, F);
  and and_2 (and_2_out, Ab, D, Eb, Fb);
  and and_3 (and_3_out, Ab, Cb, Db, Eb);
  not not_1 (Ab, A);
  not not_2 (Bb, B);
  not not_3 (Cb, C);
  not not_4 (Db, D);
  not not_5 (Eb, E);
  not not_6 (Fb, F);
  or or_1 (Before, and_1_out, and_2_out, and_3_out);
  and and_4 (and_4_out, Ab, Bb, Cb, Db, F);
  and and_5 (and_5_out, Ab, Bb, E, F);
  and and_6 (and_6_out, Ab, Cb, Eb, Fb);
  and and_7 (and_7_out, Ab, D, Eb, Fb);
  and and_8 (and_8_out, Ab, Cb, Db, Eb);
  or or_2 (After, and_5_out, and_6_out, and_4_out, and_7_out, and_8_out);
endmodule
