// Digital circuit Template.dig as structural Verilog
module Template (
  input  [7:0] In,
  output [8:0] Output
);

  wire add_1_c_o, add_2_c_o, add_3_c_o, add_4_c_o, add_5_c_o, add_6_c_o, add_7_c_o, i0b, i1b, i2b, i3b, i4b,
       i5b, i6b, i7b;

  not not_1 (i0b, In[0]);
  Add add_1 (.a(i0b), .b(1'b1), .c_i(1'b0), .s(Output[0]), .c_o(add_1_c_o));
  Add add_2 (.a(i4b), .b(1'b0), .c_i(add_7_c_o), .s(Output[4]), .c_o(add_2_c_o));
  not not_2 (i1b, In[1]);
  not not_3 (i2b, In[2]);
  Add add_3 (.a(i1b), .b(1'b0), .c_i(add_1_c_o), .s(Output[1]), .c_o(add_3_c_o));
  Add add_4 (.a(i5b), .b(1'b0), .c_i(add_2_c_o), .s(Output[5]), .c_o(add_4_c_o));
  not not_4 (i3b, In[3]);
  not not_5 (i4b, In[4]);
  Add add_5 (.a(i2b), .b(1'b0), .c_i(add_3_c_o), .s(Output[2]), .c_o(add_5_c_o));
  Add add_6 (.a(i6b), .b(1'b0), .c_i(add_4_c_o), .s(Output[6]), .c_o(add_6_c_o));
  not not_6 (i5b, In[5]);
  Add add_7 (.a(i3b), .b(1'b0), .c_i(add_5_c_o), .s(Output[3]), .c_o(add_7_c_o));
  Add add_8 (.a(i7b), .b(1'b0), .c_i(add_6_c_o), .s(Output[7]), .c_o(Output[8]));
  not not_7 (i6b, In[6]);
  not not_8 (i7b, In[7]);

  // Other names for the same wires on the sheet: i0 = In[0]; i1 = In[1]; i2 = In[2]; i3 = In[3]; i4 = In[4];
  //   i5 = In[5]; i6 = In[6]; i7 = In[7]; o0 = Output[0]; o1 = Output[1]; o2 = Output[2]; o3 = Output[3];
  //   o4 = Output[4]; o5 = Output[5]; o6 = Output[6]; o7 = Output[7]; o8 = Output[8]
endmodule
