// Digital circuit Template.dig as structural Verilog
module Template (
  input  [3:0] In,
  output [3:0] Output
);

  wire and_1_out, and_2_out, and_3_out, and_4_out, and_5_out, and_6_out, and_7_out, and_8_out, and_9_out,
       and_10_out, i0b, i1b, i2b, i3b;

  not not_1 (i0b, In[0]);
  and and_1 (and_1_out, In[0], i1b, In[3]);
  and and_2 (and_2_out, i0b, In[1]);
  and and_3 (and_3_out, In[1], i3b);
  and and_4 (and_4_out, i0b, i1b, In[2]);
  and and_5 (and_5_out, In[0], i2b, In[3]);
  and and_6 (and_6_out, In[1], i2b, In[3]);
  and and_7 (and_7_out, In[2], i3b);
  and and_8 (and_8_out, In[0], i1b, In[3]);
  and and_9 (and_9_out, In[1], i2b, In[3]);
  and and_10 (and_10_out, In[2], In[3]);
  not not_2 (i1b, In[1]);
  or or_1 (Output[1], and_1_out, and_2_out, and_3_out);
  not not_3 (i2b, In[2]);
  or or_2 (Output[2], and_4_out, and_5_out, and_6_out, and_7_out);
  or or_3 (Output[3], and_8_out, and_9_out, and_10_out);
  not not_4 (i3b, In[3]);

  assign Output[0] = In[0];

  // Other names for the same wires on the sheet: i0 = In[0]; o0 = In[0]; i1 = In[1]; i2 = In[2]; i3 = In[3];
  //   o1 = Output[1]; o2 = Output[2]; o3 = Output[3]
endmodule
