// Digital circuit lab5-4.dig as structural Verilog
module lab5_4 (
  input  [3:0] In,
  output [3:0] \output 
);

  wire add_1_c_o, add_2_c_o, add_3_c_o, i0b, i1b, i2b, i3b, s4;
  wire [3:0] Out;

  Add add_1 (.a(i0b), .b(1'b1), .c_i(1'b0), .s(Out[0]), .c_o(add_1_c_o));
  not not_1 (i0b, In[0]);
  Multiplexer #(.Bits(4)) multiplexer_1 (.sel(In[3]), .in_0(In), .in_1(Out), .out(\output ));
  not not_2 (i1b, In[1]);
  Add add_2 (.a(i1b), .b(1'b0), .c_i(add_1_c_o), .s(Out[1]), .c_o(add_2_c_o));
  not not_3 (i2b, In[2]);
  Add add_3 (.a(i2b), .b(1'b0), .c_i(add_2_c_o), .s(Out[2]), .c_o(add_3_c_o));
  not not_4 (i3b, In[3]);
  Add add_4 (.a(In[3]), .b(1'b0), .c_i(add_3_c_o), .s(Out[3]), .c_o(s4));

  // Other names for the same wires on the sheet: i0 = In[0]; i1 = In[1]; i2 = In[2]; i3 = In[3]; sel = In[3];
  //   o0 = \output [0]; o1 = \output [1]; o2 = \output [2]; o3 = \output [3]; s0 = Out[0]; s1 = Out[1]; s2 = Out[2];
  //   s3 = Out[3]
endmodule
