// Digital circuit ArithmeticFunction.dig as structural Verilog
module ArithmeticFunction (
  input  Cin,
  input  A,
  input  B,
  input  [2:0] S,
  output Cout,
  output Sum
);

  wire not_1_out, not_2_out, o0, o1;

  Multiplexer #(.Selector_Bits(3)) multiplexer_1 (
    .sel(S), .in_0(A), .in_1(A), .in_2(A), .in_3(A), .in_4(not_1_out), .in_5(1'b0), .in_6(A), .in_7(1'b0),
    .out(o0));
  not not_1 (not_1_out, A);
  Multiplexer #(.Selector_Bits(3)) multiplexer_2 (
    .sel(S), .in_0(1'b0), .in_1(1'b1), .in_2(B), .in_3(not_2_out), .in_4(1'b0), .in_5(B), .in_6(A),
    .in_7(1'b0), .out(o1));
  not not_2 (not_2_out, B);
  Add add_1 (.a(o0), .b(o1), .c_i(Cin), .s(Sum), .c_o(Cout));
endmodule
