// Digital circuit LogicalFunction.dig as structural Verilog
module LogicalFunction (
  input  A,
  input  B,
  input  [2:0] S,
  output Out
);

  wire Bb, not_2_out, o0, o1, o2, o3, o4, o5, o6;

  not not_1 (o0, A);
  nand nand_1 (o1, A, B);
  nor nor_1 (o2, A, B);
  xnor xnor_1 (o3, A, B);
  and and_1 (o4, A, B);
  or or_1 (o5, A, B);
  and and_2 (o6, A, not_2_out);
  not not_2 (not_2_out, B);
  not not_3 (Bb, B);
  Multiplexer #(.Selector_Bits(3)) multiplexer_1 (
    .sel(S), .in_0(o0), .in_1(o1), .in_2(o2), .in_3(o3), .in_4(o4), .in_5(o5), .in_6(o6), .in_7(A), .out(Out));
endmodule
