// Digital circuit Template.dig as structural Verilog
module Template (
  input  [3:0] A,
  input  [2:0] S,
  input  M,
  input  C,
  input  [3:0] B,
  output [3:0] F,
  output Cout
);

  wire and_2_out, arithmeticfunction_1_cout, arithmeticfunction_2_cout, arithmeticfunction_3_cout, Cout_t,
       CoutS, LF0, LF1, LF2, LF3, nand_1_out, S7;
  wire [3:0] o7, oS7b;

  LogicalFunction logicalfunction_1 (.A(A[0]), .B(B[0]), .S(S), .Out(LF0));
  LogicalFunction logicalfunction_2 (.A(A[1]), .B(B[1]), .S(S), .Out(LF1));
  LogicalFunction logicalfunction_3 (.A(A[2]), .B(B[2]), .S(S), .Out(LF2));
  LogicalFunction logicalfunction_4 (.A(A[3]), .B(B[3]), .S(S), .Out(LF3));
  Multiplexer #(.Bits(4)) multiplexer_1 (.sel(M), .in_0({LF3, LF2, LF1, LF0}), .in_1(o7), .out(F));
  nand nand_1 (nand_1_out, S[2], S[1]);
  and and_1 (S7, S[0], S[1], S[2]);
  and and_2 (and_2_out, nand_1_out, C);
  ArithmeticFunction arithmeticfunction_1 (
    .Cin(and_2_out), .A(A[0]), .B(B[0]), .S(S), .Cout(arithmeticfunction_1_cout), .Sum(oS7b[0]));
  Multiplexer multiplexer_2 (.sel(M), .in_0(1'b0), .in_1(Cout_t), .out(Cout));
  Multiplexer #(.Bits(4)) multiplexer_3 (.sel(S7), .in_0(oS7b), .in_1({1'b0, A[3:1]}), .out(o7));
  ArithmeticFunction arithmeticfunction_2 (
    .Cin(arithmeticfunction_1_cout), .A(A[1]), .B(B[1]), .S(S), .Cout(arithmeticfunction_2_cout),
    .Sum(oS7b[1]));
  Multiplexer multiplexer_4 (.sel(S7), .in_0(CoutS), .in_1(1'b0), .out(Cout_t));
  ArithmeticFunction arithmeticfunction_3 (
    .Cin(arithmeticfunction_2_cout), .A(A[2]), .B(B[2]), .S(S), .Cout(arithmeticfunction_3_cout),
    .Sum(oS7b[2]));
  ArithmeticFunction arithmeticfunction_4 (
    .Cin(arithmeticfunction_3_cout), .A(A[3]), .B(B[3]), .S(S), .Cout(CoutS), .Sum(oS7b[3]));

  // Other names for the same wires on the sheet: oS7[2:0] = A[3:1]; Cin = C; LFall[3:0] = {LF3, LF2, LF1, LF0};
  //   SUM0 = oS7b[0]; SUM1 = oS7b[1]; SUM2 = oS7b[2]; SUM3 = oS7b[3]
endmodule
