// Digital circuit Template.dig as structural Verilog
module Template (
  input  P,
  input  T,
  input  D,
  input  C,
  input  B,
  input  A,
  input  Clr,
  input  Load,
  input  Clock,
  output QD,
  output QC,
  output QB,
  output QA,
  output RCO
);

  wire PT;
  wire [3:0] add_1_s, multiplexer_1_out, multiplexer_2_out, multiplexer_3_out;

  and and_1 (PT, P, T);
  Add #(.Bits(4)) add_1 (.a({QD, QC, QB, QA}), .b(4'b0001), .c_i(1'b0), .s(add_1_s));  // open: c_o
  Multiplexer #(.Bits(4)) multiplexer_1 (.sel(PT), .in_0({QD, QC, QB, QA}), .in_1(add_1_s), .out(multiplexer_1_out));
  Multiplexer #(.Bits(4)) multiplexer_2 (.sel(Clr), .in_0(4'b0000), .in_1(multiplexer_1_out), .out(multiplexer_2_out));
  Multiplexer #(.Bits(4)) multiplexer_3 (
    .sel(Load), .in_0({D, C, B, A}), .in_1(multiplexer_2_out), .out(multiplexer_3_out));
  D_FF #(.Bits(4)) d_ff_1 (.D(multiplexer_3_out), .C(Clock), .Q({QD, QC, QB, QA}));  // open: nQ
  and and_2 (RCO, QA, QB, QC, QD);

  // Other names for the same wires on the sheet: QAll[3:0] = {QD, QC, QB, QA}
endmodule
