// Digital circuit Template.dig as structural Verilog
module Template (
  input  A,
  input  B,
  input  Clr,
  input  Clock,
  output Z
);

  wire add_1_s, and_2_out, cout, d_ff_1_q;

  Add add_1 (.a(A), .b(B), .c_i(d_ff_1_q), .s(add_1_s), .c_o(cout));
  and and_1 (Z, add_1_s, Clr);
  and and_2 (and_2_out, cout, Clr);
  D_FF d_ff_1 (.D(and_2_out), .C(Clock), .Q(d_ff_1_q));  // open: nQ
endmodule
