// Digital circuit Template.dig as structural Verilog
module Template (
  input  P,
  input  Clr,
  input  clock,
  output Z
);

  wire and_1_out, and_2_out, clr_t, d_ff_1_q, not_2_out;

  not not_1 (clr_t, Clr);
  not not_2 (not_2_out, d_ff_1_q);
  and and_1 (and_1_out, P, clr_t);
  and and_2 (and_2_out, not_2_out, clr_t, P);
  D_FF d_ff_1 (.D(and_1_out), .C(clock), .Q(d_ff_1_q));  // open: nQ
  D_FF d_ff_2 (.D(and_2_out), .C(clock), .Q(Z));  // open: nQ

  // Other names for the same wires on the sheet: clk = clock
endmodule
