// Digital circuit lab09.dig as structural Verilog
module lab09 (
  input  P5,
  input  reset,
  input  clock,
  input  P10,
  input  P20,
  input  Pcoffee,
  input  Ptea,
  input  Pchange,
  input  Pnext,
  output [5:0] Balance,
  output CoffeeOut,
  output TeaOut,
  output [1:0] Change5,
  output [1:0] Change10,
  output [1:0] Change20
);

  wire _0001, _0111, _1101, and_5_out, and_6_out, and_7_out, and_12_out, and_13_out, and_14_out, Balance0,
       Check5, Check10, Check20, comparator_1_lt, comparator_2_lt, comparator_3_lt, comparator_4_gt,
       comparator_5_gt, d_ff_2_nq, d_ff_3_q, d_ff_4_nq, d_ff_5_q, d_ff_6_nq, d_ff_7_q, d_ff_8_nq, d_ff_9_q,
       d_ff_10_q, d_ff_11_nq, d_ff_12_q, d_ff_13_nq, d_ff_14_q, d_ff_15_nq, d_ff_16_q, d_ff_17_q, d_ff_18_q,
       d_ff_19_q, d_ff_20_q, d_ff_21_q, d_ff_22_q, d_ff_23_q, d_ff_24_nq, eChange5, eChange10, eChange20,
       lt_10, lt_20, not_1_out, not_2_out, not_3_out, not_4_out, not_5_out, oCoffee, or_2_out, or_3_out,
       oTea, OutChange, OutNext, rs_ff_as_1_q, rs_ff_as_2_q, rs_ff_as_3_q;
  wire [5:0] add_1_s, BalanceChanged, lookuptable_1_out, multiplexer_1_out, multiplexer_2_out, Option_out;

  Comparator #(.Bits(6)) comparator_1 (.a(Balance), .b(6'b101110), .lt(comparator_1_lt));  // open: gt, eq
  Comparator #(.Bits(6)) comparator_2 (.a(Balance), .b(6'b101001), .lt(comparator_2_lt));  // open: gt, eq
  Comparator #(.Bits(6)) comparator_3 (.a(Balance), .b(6'b011111), .lt(comparator_3_lt));  // open: gt, eq
  Comparator #(.Bits(6)) comparator_4 (.a(Balance), .b(6'b011000), .gt(comparator_4_gt));  // open: eq, lt
  Comparator #(.Bits(6)) comparator_5 (.a(Balance), .b(6'b010011), .gt(comparator_5_gt));  // open: eq, lt
  D_FF d_ff_1 (.D(Pnext), .C(clock));  // open: Q, nQ
  not not_1 (not_1_out, CoffeeOut);
  not not_2 (not_2_out, TeaOut);
  or or_1 (_0111, CoffeeOut, TeaOut);
  and and_1 (_0001, not_1_out, not_2_out);
  and and_2 (Check5, _0001, P5, comparator_1_lt);
  and and_3 (Check10, _0001, P10, comparator_2_lt);
  and and_4 (Check20, _0001, P20, comparator_3_lt);
  and and_5 (and_5_out, comparator_4_gt, Pcoffee, _0001);
  and and_6 (and_6_out, comparator_5_gt, Ptea, _0001);
  and and_7 (and_7_out, Pnext, _0111);
  D_FF d_ff_2 (.D(Pchange), .C(clock), .nQ(d_ff_2_nq));  // open: Q
  D_FF d_ff_3 (.D(Pchange), .C(clock), .Q(d_ff_3_q));  // open: nQ
  D_FF d_ff_4 (.D(and_5_out), .C(clock), .nQ(d_ff_4_nq));  // open: Q
  D_FF d_ff_5 (.D(and_5_out), .C(clock), .Q(d_ff_5_q));  // open: nQ
  D_FF d_ff_6 (.D(and_6_out), .C(clock), .nQ(d_ff_6_nq));  // open: Q
  D_FF d_ff_7 (.D(and_6_out), .C(clock), .Q(d_ff_7_q));  // open: nQ
  D_FF d_ff_8 (.D(and_7_out), .C(clock), .nQ(d_ff_8_nq));  // open: Q
  D_FF d_ff_9 (.D(and_7_out), .C(clock), .Q(d_ff_9_q));  // open: nQ
  D_FF d_ff_10 (.D(d_ff_2_nq), .C(clock), .Q(d_ff_10_q));  // open: nQ
  D_FF d_ff_11 (.D(Check5), .C(clock), .nQ(d_ff_11_nq));  // open: Q
  D_FF d_ff_12 (.D(Check5), .C(clock), .Q(d_ff_12_q));  // open: nQ
  D_FF d_ff_13 (.D(Check10), .C(clock), .nQ(d_ff_13_nq));  // open: Q
  D_FF d_ff_14 (.D(Check10), .C(clock), .Q(d_ff_14_q));  // open: nQ
  D_FF d_ff_15 (.D(Check20), .C(clock), .nQ(d_ff_15_nq));  // open: Q
  D_FF d_ff_16 (.D(Check20), .C(clock), .Q(d_ff_16_q));  // open: nQ
  and and_8 (OutChange, d_ff_10_q, d_ff_3_q);
  D_FF d_ff_17 (.D(d_ff_4_nq), .C(clock), .Q(d_ff_17_q));  // open: nQ
  D_FF d_ff_18 (.D(d_ff_6_nq), .C(clock), .Q(d_ff_18_q));  // open: nQ
  D_FF d_ff_19 (.D(d_ff_8_nq), .C(clock), .Q(d_ff_19_q));  // open: nQ
  D_FF d_ff_20 (.D(d_ff_11_nq), .C(clock), .Q(d_ff_20_q));  // open: nQ
  D_FF d_ff_21 (.D(d_ff_13_nq), .C(clock), .Q(d_ff_21_q));  // open: nQ
  D_FF d_ff_22 (.D(d_ff_15_nq), .C(clock), .Q(d_ff_22_q));  // open: nQ
  and and_9 (oCoffee, d_ff_17_q, d_ff_5_q);
  and and_10 (oTea, d_ff_18_q, d_ff_7_q);
  and and_11 (OutNext, d_ff_19_q, d_ff_9_q);
  and and_12 (and_12_out, d_ff_20_q, d_ff_12_q);
  and and_13 (and_13_out, d_ff_21_q, d_ff_14_q);
  and and_14 (and_14_out, d_ff_22_q, d_ff_16_q);
  not not_3 (not_3_out, lt_20);
  and and_15 (eChange20, not_3_out, _1101);
  CounterPreset #(.maxValue(2), .Bits(2)) counterpreset_1 (
    .en(eChange20), .C(clock), .dir(1'b0), .in(2'b00), .ld(1'b0), .clr(or_2_out), .out(Change20));  // open: ovf
  D_FF d_ff_23 (.D(OutChange), .C(clock), .Q(d_ff_23_q));  // open: nQ
  Comparator #(.Bits(6)) comparator_6 (.a(Balance), .b(6'b010100), .lt(lt_20));  // open: gt, eq
  Comparator #(.Bits(6)) comparator_7 (.a(Balance), .b(6'b001010), .lt(lt_10));  // open: gt, eq
  Comparator #(.Bits(6)) comparator_8 (.a(Balance), .b(6'b000101), .lt(Balance0));  // open: gt, eq
  LookUpTable #(.Bits(6)) Option (
    .in0(and_12_out), .in1(and_13_out), .in2(and_14_out), .in3(oCoffee), .in4(oTea), .out(Option_out));
  RS_FF_AS rs_ff_as_1 (.S(d_ff_23_q), .R(Balance0), .Q(rs_ff_as_1_q));  // open: nQ
  not not_4 (not_4_out, lt_10);
  or or_2 (or_2_out, OutChange, reset);
  Add #(.Bits(6)) add_1 (.a(Balance), .b(Option_out), .c_i(1'b0), .s(add_1_s));  // open: c_o
  LookUpTable #(.Bits(6)) lookuptable_1 (.in0(lt_20), .in1(lt_10), .in2(Balance0), .out(lookuptable_1_out));
  and and_16 (eChange10, lt_20, not_4_out, _1101);
  CounterPreset #(.Bits(2)) counterpreset_2 (
    .en(eChange10), .C(clock), .dir(1'b0), .in(2'b00), .ld(1'b0), .clr(or_2_out), .out(Change10));  // open: ovf
  D_FF d_ff_24 (.D(rs_ff_as_1_q), .C(clock), .Q(_1101), .nQ(d_ff_24_nq));
  Multiplexer #(.Bits(6)) multiplexer_1 (
    .sel(d_ff_24_nq), .in_0(BalanceChanged), .in_1(add_1_s), .out(multiplexer_1_out));
  Sub #(.Bits(6)) sub_1 (.a(Balance), .b(lookuptable_1_out), .c_i(1'b0), .s(BalanceChanged));  // open: c_o
  Multiplexer #(.Bits(6)) multiplexer_2 (
    .sel(reset), .in_0(multiplexer_1_out), .in_1({6{1'b0}}), .out(multiplexer_2_out));
  or or_3 (or_3_out, OutChange, OutNext, reset);
  and and_17 (eChange5, lt_20, lt_10, not_5_out, _1101);
  not not_5 (not_5_out, Balance0);
  CounterPreset #(.Bits(2)) counterpreset_3 (
    .en(eChange5), .C(clock), .dir(1'b0), .in(2'b00), .ld(1'b0), .clr(or_2_out), .out(Change5));  // open: ovf
  D_FF #(.Bits(6)) d_ff_25 (.D(multiplexer_2_out), .C(clock), .Q(Balance));  // open: nQ
  RS_FF_AS rs_ff_as_2 (.S(oCoffee), .R(or_3_out), .Q(rs_ff_as_2_q));  // open: nQ
  RS_FF_AS rs_ff_as_3 (.S(oTea), .R(or_3_out), .Q(rs_ff_as_3_q));  // open: nQ
  D_FF d_ff_26 (.D(rs_ff_as_2_q), .C(clock), .Q(CoffeeOut));  // open: nQ
  D_FF d_ff_27 (.D(rs_ff_as_3_q), .C(clock), .Q(TeaOut));  // open: nQ

  // Notes on the sheet:
  //   contents of Option (hex, n*v repeats v):
  //   0,5,a,0,14,0,0,0,ffffffffffffffe7,7*0,ffffffffffffffec
  //   contents of lookuptable_1 (hex, n*v repeats v):
  //   14,a,0,5
endmodule
