// Digital circuit lab09_100.dig as structural Verilog
module lab09_100 (
  input  P5,
  input  reset,
  input  clock,
  input  P10,
  input  P20,
  input  Pcoffee,
  input  Ptea,
  input  Pchange,
  input  Pnext,
  output [5:0] Balance,
  output CoffeeOut,
  output TeaOut,
  output [1:0] Change5,
  output [1:0] Change10,
  output [1:0] Change20
);

  wire _0001, _0111, _1101, Balance0, Check5, Check10, Check20, CheckCoffee, CheckNext, CheckTea,
       comparator_1_lt, comparator_2_lt, comparator_3_lt, comparator_4_gt, comparator_5_gt, d_ff_2_nq,
       d_ff_3_q, d_ff_4_q, d_ff_5_nq, d_ff_6_q, d_ff_7_nq, d_ff_8_q, d_ff_9_nq, d_ff_10_q, d_ff_11_nq,
       d_ff_12_q, d_ff_13_nq, d_ff_14_q, d_ff_15_nq, d_ff_16_q, d_ff_17_q, d_ff_18_q, d_ff_19_q, d_ff_20_q,
       d_ff_21_q, d_ff_22_q, d_ff_23_q, d_ff_24_nq, eChange5, eChange10, eChange20, lt_10, lt_20, not_1_out,
       not_2_out, not_3_out, not_4_out, not_5_out, or_2_out, or_3_out, Out5, Out10, Out20, OutChange,
       OutCoffee, OutNext, OutTea, rs_ff_as_1_q, rs_ff_as_2_q, rs_ff_as_3_q;
  wire [5:0] add_1_s, BalanceChanged, lookuptable_1_out, multiplexer_1_out, multiplexer_2_out, Option_out;

  Comparator #(.Bits(6)) comparator_1 (.a(Balance), .b(6'b101110), .lt(comparator_1_lt));  // open: gt, eq
  Comparator #(.Bits(6)) comparator_2 (.a(Balance), .b(6'b101001), .lt(comparator_2_lt));  // open: gt, eq
  Comparator #(.Bits(6)) comparator_3 (.a(Balance), .b(6'b011111), .lt(comparator_3_lt));  // open: gt, eq
  Comparator #(.Bits(6)) comparator_4 (.a(Balance), .b(6'b011000), .gt(comparator_4_gt));  // open: eq, lt
  Comparator #(.Bits(6)) comparator_5 (.a(Balance), .b(6'b010011), .gt(comparator_5_gt));  // open: eq, lt
  D_FF d_ff_1 (.D(Pnext), .C(clock));  // open: Q, nQ
  not not_1 (not_1_out, CoffeeOut);
  not not_2 (not_2_out, TeaOut);
  and and_1 (_0001, not_1_out, not_2_out);
  and and_2 (Check5, _0001, P5, comparator_1_lt);
  and and_3 (Check10, _0001, P10, comparator_2_lt);
  and and_4 (Check20, _0001, P20, comparator_3_lt);
  and and_5 (CheckCoffee, comparator_4_gt, Pcoffee, _0001);
  and and_6 (CheckTea, comparator_5_gt, Ptea, _0001);
  and and_7 (CheckNext, Pnext, _0111);
  D_FF d_ff_2 (.D(Pchange), .C(clock), .nQ(d_ff_2_nq));  // open: Q
  D_FF d_ff_3 (.D(Pchange), .C(clock), .Q(d_ff_3_q));  // open: nQ
  D_FF d_ff_4 (.D(d_ff_2_nq), .C(clock), .Q(d_ff_4_q));  // open: nQ
  and and_8 (OutChange, d_ff_4_q, d_ff_3_q);
  or or_1 (_0111, CoffeeOut, TeaOut);
  D_FF d_ff_5 (.D(Check5), .C(clock), .nQ(d_ff_5_nq));  // open: Q
  D_FF d_ff_6 (.D(Check5), .C(clock), .Q(d_ff_6_q));  // open: nQ
  D_FF d_ff_7 (.D(Check10), .C(clock), .nQ(d_ff_7_nq));  // open: Q
  D_FF d_ff_8 (.D(Check10), .C(clock), .Q(d_ff_8_q));  // open: nQ
  D_FF d_ff_9 (.D(Check20), .C(clock), .nQ(d_ff_9_nq));  // open: Q
  D_FF d_ff_10 (.D(Check20), .C(clock), .Q(d_ff_10_q));  // open: nQ
  D_FF d_ff_11 (.D(CheckCoffee), .C(clock), .nQ(d_ff_11_nq));  // open: Q
  D_FF d_ff_12 (.D(CheckCoffee), .C(clock), .Q(d_ff_12_q));  // open: nQ
  D_FF d_ff_13 (.D(CheckTea), .C(clock), .nQ(d_ff_13_nq));  // open: Q
  D_FF d_ff_14 (.D(CheckTea), .C(clock), .Q(d_ff_14_q));  // open: nQ
  D_FF d_ff_15 (.D(CheckNext), .C(clock), .nQ(d_ff_15_nq));  // open: Q
  D_FF d_ff_16 (.D(CheckNext), .C(clock), .Q(d_ff_16_q));  // open: nQ
  D_FF d_ff_17 (.D(d_ff_5_nq), .C(clock), .Q(d_ff_17_q));  // open: nQ
  D_FF d_ff_18 (.D(d_ff_7_nq), .C(clock), .Q(d_ff_18_q));  // open: nQ
  D_FF d_ff_19 (.D(d_ff_9_nq), .C(clock), .Q(d_ff_19_q));  // open: nQ
  D_FF d_ff_20 (.D(d_ff_11_nq), .C(clock), .Q(d_ff_20_q));  // open: nQ
  D_FF d_ff_21 (.D(d_ff_13_nq), .C(clock), .Q(d_ff_21_q));  // open: nQ
  D_FF d_ff_22 (.D(d_ff_15_nq), .C(clock), .Q(d_ff_22_q));  // open: nQ
  and and_9 (Out5, d_ff_17_q, d_ff_6_q);
  and and_10 (Out10, d_ff_18_q, d_ff_8_q);
  and and_11 (Out20, d_ff_19_q, d_ff_10_q);
  and and_12 (OutCoffee, d_ff_20_q, d_ff_12_q);
  and and_13 (OutTea, d_ff_21_q, d_ff_14_q);
  and and_14 (OutNext, d_ff_22_q, d_ff_16_q);
  D_FF d_ff_23 (.D(OutChange), .C(clock), .Q(d_ff_23_q));  // open: nQ
  Comparator #(.Bits(6)) comparator_6 (.a(Balance), .b(6'b010100), .lt(lt_20));  // open: gt, eq
  Comparator #(.Bits(6)) comparator_7 (.a(Balance), .b(6'b001010), .lt(lt_10));  // open: gt, eq
  Comparator #(.Bits(6)) comparator_8 (.a(Balance), .b(6'b000101), .lt(Balance0));  // open: gt, eq
  LookUpTable #(.Bits(6)) lookuptable_1 (.in0(lt_20), .in1(lt_10), .in2(Balance0), .out(lookuptable_1_out));
  LookUpTable #(.Bits(6)) Option (
    .in0(Out5), .in1(Out10), .in2(Out20), .in3(OutCoffee), .in4(OutTea), .out(Option_out));
  or or_2 (or_2_out, OutChange, OutNext, reset);
  Sub #(.Bits(6)) sub_1 (.a(Balance), .b(lookuptable_1_out), .c_i(1'b0), .s(BalanceChanged));  // open: c_o
  RS_FF_AS rs_ff_as_1 (.S(d_ff_23_q), .R(Balance0), .Q(rs_ff_as_1_q));  // open: nQ
  Add #(.Bits(6)) add_1 (.a(Balance), .b(Option_out), .c_i(1'b0), .s(add_1_s));  // open: c_o
  D_FF d_ff_24 (.D(rs_ff_as_1_q), .C(clock), .Q(_1101), .nQ(d_ff_24_nq));
  RS_FF_AS rs_ff_as_2 (.S(OutCoffee), .R(or_2_out), .Q(rs_ff_as_2_q));  // open: nQ
  RS_FF_AS rs_ff_as_3 (.S(OutTea), .R(or_2_out), .Q(rs_ff_as_3_q));  // open: nQ
  not not_3 (not_3_out, lt_20);
  and and_15 (eChange20, not_3_out, _1101);
  CounterPreset #(.maxValue(2), .Bits(2)) counterpreset_1 (
    .en(eChange20), .C(clock), .dir(1'b0), .in(2'b00), .ld(1'b0), .clr(or_3_out), .out(Change20));  // open: ovf
  Multiplexer #(.Bits(6)) multiplexer_1 (
    .sel(d_ff_24_nq), .in_0(BalanceChanged), .in_1(add_1_s), .out(multiplexer_1_out));
  D_FF d_ff_25 (.D(rs_ff_as_2_q), .C(clock), .Q(CoffeeOut));  // open: nQ
  D_FF d_ff_26 (.D(rs_ff_as_3_q), .C(clock), .Q(TeaOut));  // open: nQ
  Multiplexer #(.Bits(6)) multiplexer_2 (
    .sel(reset), .in_0(multiplexer_1_out), .in_1({6{1'b0}}), .out(multiplexer_2_out));
  D_FF #(.Bits(6)) d_ff_27 (.D(multiplexer_2_out), .C(clock), .Q(Balance));  // open: nQ
  and and_16 (eChange10, lt_20, not_4_out, _1101);
  not not_4 (not_4_out, lt_10);
  or or_3 (or_3_out, OutChange, reset);
  CounterPreset #(.Bits(2)) counterpreset_2 (
    .en(eChange10), .C(clock), .dir(1'b0), .in(2'b00), .ld(1'b0), .clr(or_3_out), .out(Change10));  // open: ovf
  not not_5 (not_5_out, Balance0);
  and and_17 (eChange5, lt_20, lt_10, not_5_out, _1101);
  CounterPreset #(.Bits(2)) counterpreset_3 (
    .en(eChange5), .C(clock), .dir(1'b0), .in(2'b00), .ld(1'b0), .clr(or_3_out), .out(Change5));  // open: ovf

  // Notes on the sheet:
  //   contents of lookuptable_1 (hex, n*v repeats v):
  //   14,a,0,5
  //   contents of Option (hex, n*v repeats v):
  //   0,5,a,0,14,0,0,0,ffffffffffffffe7,7*0,ffffffffffffffec
endmodule
