// Digital circuit lab10.dig as structural Verilog
module lab10 (
  input  [8:0] N,
  input  reset,
  input  start,
  input  clock,
  output done,
  output [7:0] displayout,
  output [15:0] clockcount,
  output valid
);

  wire and_2_out, and_3_out, and_4_out, and_5_out, and_6_out, and_10_out, comparator_3_eq, doneRAM, doneROM,
       enCounter, enWriting, not_1_out, not_2_out, not_3_out, not_4_out, not_5_out, or_1_out, strRAM, valid_t;
  wire [7:0] dataROM, dataTempAdd, RAMCounter;
  wire [8:0] counterRAMTemp, counterROM;
  wire [9:0] dataTemp, dataTemp_plus, dataTemp_t, dataTempIn;

  Comparator #(.Bits(10)) comparator_1 (.a(dataTemp), .b({10{1'b0}}), .gt(valid_t));  // open: eq, lt
  and and_1 (strRAM, valid_t, doneROM, ~doneRAM);  // And
  Comparator #(.Bits(9)) comparator_2 (.a(counterRAMTemp), .b(N), .eq(doneRAM));  // open: gt, lt
  not not_1 (not_1_out, doneRAM);
  Comparator #(.Bits(10)) comparator_3 (.a(dataTemp), .b({10{1'b0}}), .eq(comparator_3_eq));  // open: gt, lt
  RS_FF rs_ff_1 (.S(start), .C(clock), .R(reset), .Q(enCounter));  // open: nQ
  Comparator #(.Bits(9)) comparator_4 (.a(counterROM), .b(N), .eq(doneROM));  // open: gt, lt
  Counter #(.Bits(9)) u_CounterRom (.en(enWriting), .C(clock), .clr(reset), .out(counterROM));  // open: ovf
  and and_2 (and_2_out, enCounter, ~doneROM);  // And
  and and_3 (and_3_out, enCounter, ~doneROM);  // And
  not not_2 (not_2_out, doneRAM);
  and and_4 (and_4_out, enCounter, doneROM, not_1_out, comparator_3_eq);
  and and_5 (and_5_out, strRAM, enCounter);
  and and_6 (and_6_out, enCounter, doneROM, not_2_out, valid_t);
  Seven_Seg_Hex seven_seg_hex_1 (.d(displayout[7:4]), .dp(1'b0));
  assign displayout = and_5_out ? dataTempAdd : 8'bz;  // Driver driver_1
  or or_1 (or_1_out, strRAM, and_3_out);
  Counter #(.Bits(8)) u_RAMCounter (.en(and_4_out), .C(clock), .clr(reset), .out(RAMCounter));  // open: ovf
  Seven_Seg_Hex seven_seg_hex_2 (.d(displayout[3:0]), .dp(1'b0));
  Counter #(.Bits(9)) RAMTempCounter (.en(and_6_out), .C(clock), .clr(reset), .out(counterRAMTemp));  // open: ovf
  ROM #(.AddrBits(9), .isProgramMemory("true"), .Bits(8)) ROMFILE (.A(counterROM), .sel(and_2_out), .D(dataROM));
  Multiplexer #(.Bits(8)) multiplexer_1 (.sel(doneROM), .in_0(dataROM), .in_1(RAMCounter), .out(dataTempAdd));
  not not_3 (not_3_out, doneROM);
  RAMDualPort #(.AddrBits(8), .Bits(10)) RAMTemp (
    .A(dataTempAdd), .Din(dataTempIn), .str(or_1_out), .C(clock), .ld(1'b1), .D(dataTemp));
  and and_7 (enWriting, enCounter, not_3_out);
  not not_4 (not_4_out, clock);
  RAMDualPort #(.AddrBits(9), .Bits(8)) RAM (
    .A(counterRAMTemp), .Din(dataTempAdd), .str(strRAM), .C(not_4_out), .ld(1'b1));  // open: D
  Add #(.Bits(10)) add_1 (.a(dataTemp), .b(10'h1), .c_i(1'b0), .s(dataTemp_plus));  // open: c_o
  Sub #(.Bits(10)) sub_1 (.a(dataTemp), .b(10'h1), .c_i(1'b0), .s(dataTemp_t));  // open: c_o
  Multiplexer #(.Bits(10)) multiplexer_2 (.sel(doneROM), .in_0(dataTemp_plus), .in_1(dataTemp_t), .out(dataTempIn));
  and and_8 (valid, valid_t, doneROM);
  and and_9 (done, enCounter, doneRAM);
  and and_10 (and_10_out, enCounter, not_5_out);
  not not_5 (not_5_out, doneRAM);
  Counter #(.Bits(16)) counter_1 (.en(and_10_out), .C(clock), .clr(reset), .out(clockcount));  // open: ovf

  // Other names for the same wires on the sheet: oClockcount[15:0] = clockcount; oDone = done; oValid = valid;
  //   validData[7:0] = displayout

  // Notes on the sheet:
  //   contents of ROMFILE (hex, n*v repeats v):
  //   4,2,2,5,2
endmodule
