// Digital circuit 2021_final_2_stated.dig as structural Verilog
module _2021_final_2_stated (
  input  Increase,
  input  clk,
  output [2:0] out_3
);

  wire comparator_1_eq, d_ff_as_1_q, IncreaseSig;
  wire [2:0] multiplexer_1_out, NextState;
  wire [3:0] multiplexer_3_out;

  D_FF_AS d_ff_as_1 (.Set(1'b0), .D(1'b1), .C(Increase), .Clr(IncreaseSig), .Q(d_ff_as_1_q));  // open: nQ
  Multiplexer #(.Bits(3), .Selector_Bits(3)) multiplexer_1 (
    .sel(out_3), .in_0(3'b001), .in_1(3'b010), .in_2(3'b011), .in_3(3'b100), .in_4(3'b000), .in_5(3'b000),
    .in_6(3'b000), .in_7(3'b000), .out(multiplexer_1_out));
  D_FF_AS d_ff_as_2 (.Set(1'b0), .D(d_ff_as_1_q), .C(clk), .Clr(1'b0), .Q(IncreaseSig));  // open: nQ
  Multiplexer #(.Bits(3)) multiplexer_2 (.sel(IncreaseSig), .in_0(out_3), .in_1(multiplexer_1_out), .out(NextState));
  D_FF #(.Bits(3)) d_ff_1 (.D(NextState), .C(clk), .Q(out_3));  // open: nQ
  Comparator #(.Bits(3)) comparator_1 (.a(out_3), .b(3'b100), .eq(comparator_1_eq));  // open: gt, lt
  Multiplexer #(.Selector_Bits(3), .Bits(4)) multiplexer_3 (
    .sel(out_3), .in_0(4'b0011), .in_1(4'b0110), .in_2(4'b1001), .in_3(4'b1100), .in_4(4'b1111),
    .in_5(4'b1111), .in_6(4'b1111), .in_7(4'b1111), .out(multiplexer_3_out));
  LED led_1 (.in(comparator_1_eq));
  Seven_Seg_Hex seven_seg_hex_1 (.d(multiplexer_3_out), .dp(1'b0));

  // Other names for the same wires on the sheet: CurrentState[2:0] = out_3

  // Notes on the sheet:
  //   Next State Logic
  //   State Memory
  //   Output Logic
endmodule
