// Digital circuit mid1.dig as structural Verilog
module mid1 (
  input  in_1,
  input  in_2,
  input  in_3,
  input  in_4,
  input  in_5,
  input  in_6
);

  wire A, A0b, A1b, A2b, add_1_c_o, add_2_c_o, and_1_out, B0b, B1b, B2b, S0, S0b, S1, S1b, S2, S2b, S3, S3b;

  not not_1 (A2b, in_3);
  not not_2 (B2b, in_6);
  Add add_1 (.a(in_1), .b(in_4), .c_i(1'b0), .s(S0), .c_o(add_1_c_o));
  and and_1 (and_1_out, S2b, S1b);
  not not_3 (S0b, S0);
  or or_1 (A, and_1_out, S3b);
  not not_4 (A1b, in_2);
  not not_5 (B1b, in_5);
  Seven_Seg seven_seg_1 (.a(A), .b(1'b1), .c(1'b1), .d(A), .e(A), .f(A), .g(1'b0), .dp(1'b0));
  Add add_2 (.a(in_2), .b(in_5), .c_i(add_1_c_o), .s(S1), .c_o(add_2_c_o));
  not not_6 (A0b, in_1);
  not not_7 (B0b, in_4);
  not not_8 (S1b, S1);
  Add add_3 (.a(in_3), .b(in_6), .c_i(add_2_c_o), .s(S2), .c_o(S3));
  not not_9 (S2b, S2);
  not not_10 (S3b, S3);

  // Other names for the same wires on the sheet: A0 = in_1; A1 = in_2; A2 = in_3; B0 = in_4; B1 = in_5; B2 = in_6;
  //   D = A; E = A; F = A
endmodule
