// Digital circuit mid2.dig as structural Verilog
module mid2 (
  input  in_1,
  input  in_2,
  input  in_3,
  output out_4,
  output out_5
);

  wire D0, D1, D2, D3, D4, D5, D6, D7, S0b, S1b, S2b;

  not not_1 (S0b, in_1);
  Decoder #(.Selector_Bits(3)) decoder_1 (
    .sel({in_1, in_2, in_3}), .out_0(D0), .out_1(D1), .out_2(D2), .out_3(D3), .out_4(D4), .out_5(D5),
    .out_6(D6), .out_7(D7));
  not not_2 (S1b, in_2);
  or or_1 (out_4, D2, D4, D5, D6);
  or or_2 (out_5, D0, D2, D4, D6, D7);
  not not_3 (S2b, in_3);

  // Other names for the same wires on the sheet: O1 = out_4; O2 = out_5; S0 = in_1; S1 = in_2; S2 = in_3
endmodule
